// Logisim project nandcpu.circ as structural Verilog: 5 circuits, main circuit Main
module Stage_Counter (
  input  Clock,
  input  Reset,
  output [1:0] Pin_0,
  output [1:0] Pin_1,
  output [1:0] Pin_2,
  output [1:0] Pin_3,
  output [1:0] Pin_4,
  output [1:0] Pin_5,
  output [1:0] Pin_6
);

  wire [3:0] counter_1_q;

  Counter #(.width(4), .max('h7), .trigger("falling")) counter_1 (
    .Q(counter_1_q), .clk(Clock), .clr(Reset));  // open: load, D, count, carry
  Comparator #(.width(4)) comparator_1 (.a(4'b0000), .b(counter_1_q), .eq(Pin_0[1]));  // open: gt, lt
  Comparator #(.width(4)) comparator_2 (.a(4'b0001), .b(counter_1_q), .eq(Pin_1[1]));  // open: gt, lt
  Comparator #(.width(4)) comparator_3 (.a(4'b0010), .b(counter_1_q), .eq(Pin_2[1]));  // open: gt, lt
  Comparator #(.width(4)) comparator_4 (.a(4'b0011), .b(counter_1_q), .eq(Pin_3[1]));  // open: gt, lt
  Comparator #(.width(4)) comparator_5 (.a(4'b0100), .b(counter_1_q), .eq(Pin_4[1]));  // open: gt, lt
  Comparator #(.width(4)) comparator_6 (.a(4'b0101), .b(counter_1_q), .eq(Pin_5[1]));  // open: gt, lt
  Comparator #(.width(4)) comparator_7 (.a(4'b0110), .b(counter_1_q), .eq(Pin_6[1]));  // open: gt, lt
  and and_1 (Pin_0[0], Clock, Pin_0[1]);
  and and_2 (Pin_1[0], Clock, Pin_1[1]);
  and and_3 (Pin_2[0], Clock, Pin_2[1]);
  and and_4 (Pin_3[0], Clock, Pin_3[1]);
  and and_5 (Pin_4[0], Clock, Pin_4[1]);
  and and_6 (Pin_5[0], Clock, Pin_5[1]);
  and and_7 (Pin_6[0], Clock, Pin_6[1]);
endmodule

module Main (
);

  wire ALU, bit_extractor_1_out_3, bit_extractor_2_out_3, Clock, not_1_out, not_2_out, Op_1, Op_2, or_1_out,
       Reset;
  wire [1:0] Fetch__Op_1, Fetch__Result, Fetch_OldValue, Fetch_Op_1, Fetch_Op_2, Writeback;
  wire [1:1] Fetch__Op_2;
  wire [3:0] Op_1_Bit, Op_2_Bit, Result_Bit;
  wire [11:0] controlled_buffer_1_out, Op_1_Addr, Op_2_Addr, PC, Result_Addr;
  wire [15:0] MemBusIn, MemBusOut, OldValue, ram_1_data, register_1_q, register_2_q, register_3_q;

  Button button_1 (.out(Reset));
  Clock clock_1 (.out(Clock));
  Stage_Counter stage_counter_1 (
    .Clock(Clock), .Reset(Reset), .Pin_0(Fetch__Op_1), .Pin_1({Fetch__Op_2[1], Fetch__Op_1[1]}),
    .Pin_2(Fetch__Result), .Pin_3(Fetch_Op_1), .Pin_4(Fetch_Op_2), .Pin_5(Fetch_OldValue), .Pin_6(Writeback));
  assign controlled_buffer_1_out = Fetch__Op_1[1] ? PC : 12'bz;  // Controlled_Buffer controlled_buffer_1
  assign controlled_buffer_1_out = Fetch__Op_2[1] ? PC : 12'bz;  // Controlled_Buffer controlled_buffer_2
  assign controlled_buffer_1_out = Fetch__Result[1] ? PC : 12'bz;  // Controlled_Buffer controlled_buffer_3
  assign controlled_buffer_1_out = Fetch_Op_1[1] ? Op_1_Addr : 12'bz;  // Controlled_Buffer controlled_buffer_4
  assign controlled_buffer_1_out = Fetch_Op_2[1] ? Op_2_Addr : 12'bz;  // Controlled_Buffer controlled_buffer_5
  assign controlled_buffer_1_out = Fetch_OldValue[1] ? Result_Addr : 12'bz;  // Controlled_Buffer controlled_buffer_6
  assign controlled_buffer_1_out = Writeback[1] ? Result_Addr : 12'bz;  // Controlled_Buffer controlled_buffer_7
  Bit_Extractor bit_extractor_1 (.Bit_Select(Op_1_Bit), .Data(MemBusOut), .out_3(bit_extractor_1_out_3));
  Bit_Extractor bit_extractor_2 (.Bit_Select(Op_2_Bit), .Data(MemBusOut), .out_3(bit_extractor_2_out_3));
  or or_1 (or_1_out, Fetch__Op_1[0], Fetch__Op_2[1], Fetch__Result[1]);
  Register #(.width(16)) register_1 (.D(MemBusOut), .Q(register_1_q), .clk(Fetch__Op_1[0]), .clr(Reset));  // open: en
  Addresssplitter addresssplitter_1 (.Data_In(register_1_q), .Bit_Out(Op_1_Bit), .Address_Out(Op_1_Addr));
  Register #(.width(16)) register_2 (.D(MemBusOut), .Q(register_2_q), .clk(Fetch__Op_1[1]), .clr(Reset));  // open: en
  Addresssplitter addresssplitter_2 (.Data_In(register_2_q), .Bit_Out(Op_2_Bit), .Address_Out(Op_2_Addr));
  Register #(.width(16)) register_3 (.D(MemBusOut), .Q(register_3_q), .clk(Fetch__Result[0]), .clr(Reset));  // open: en
  Addresssplitter addresssplitter_3 (.Data_In(register_3_q), .Bit_Out(Result_Bit), .Address_Out(Result_Addr));
  Register #(.width(1)) register_4 (.D(bit_extractor_1_out_3), .Q(Op_1), .clk(Fetch_Op_1[0]), .clr(Reset));  // open: en
  Register #(.width(1)) register_5 (.D(bit_extractor_2_out_3), .Q(Op_2), .clk(Fetch_Op_2[0]), .clr(Reset));  // open: en
  Register #(.width(16)) register_6 (.D(MemBusOut), .Q(OldValue), .clk(Fetch_OldValue[0]), .clr(Reset));  // open: en
  Counter #(.width(12), .max('hfff), .trigger("falling")) counter_1 (
    .Q(PC), .clk(or_1_out), .clr(Reset));  // open: load, D, count, carry
  RAM #(.addrWidth(12), .dataWidth(16)) ram_1 (
    .addr(controlled_buffer_1_out), .data(ram_1_data), .clk(Clock), .ld(not_1_out));  // open: sel, clr
  assign ram_1_data = Writeback[1] ? MemBusIn : 16'bz;  // Controlled_Buffer controlled_buffer_8
  not not_1 (not_1_out, Writeback[1]);
  assign MemBusOut = not_2_out ? ram_1_data : 16'bz;  // Controlled_Buffer controlled_buffer_9
  not not_2 (not_2_out, Writeback[1]);
  Bit_Injector bit_injector_1 (.Bit(ALU), .Bit_Select(Result_Bit), .Data(OldValue), .out_4(MemBusIn));
  nand nand_1 (ALU, Op_1, Op_2);

  // Other names for the same wires on the sheet: Fetch__Op_2[0] = Fetch__Op_1[1]
endmodule

module Addresssplitter (
  input  [15:0] Data_In,
  output [3:0] Bit_Out,
  output [11:0] Address_Out
);


  assign Address_Out = Data_In[15:4];
  assign Bit_Out = Data_In[3:0];
endmodule

module Bit_Extractor (
  input  [3:0] Bit_Select,
  input  [15:0] Data,
  output out_3
);

  wire [15:0] and_1_out, shifter_1_out;

  Shifter #(.width(16)) shifter_1 (.in(16'h1), .\dist (Bit_Select), .out(shifter_1_out));
  assign and_1_out = shifter_1_out & Data;  // AND_Gate and_1, 16 bits wide
  or or_1 (out_3, and_1_out[0], and_1_out[1], and_1_out[2], and_1_out[3], and_1_out[4], and_1_out[5], and_1_out[6], and_1_out[7], and_1_out[8], and_1_out[9], and_1_out[10], and_1_out[11], and_1_out[12], and_1_out[13], and_1_out[14], and_1_out[15]);
endmodule

module Bit_Injector (
  input  Bit,
  input  [3:0] Bit_Select,
  input  [15:0] Data,
  output [15:0] out_4
);

  wire not_1_out;
  wire [15:0] and_1_out, controlled_buffer_1_out, Mask, not_2_out;

  not not_1 (not_1_out, Bit);
  assign not_2_out = ~Mask;  // NOT_Gate not_2, 16 bits wide
  assign controlled_buffer_1_out = Bit ? Mask : 16'bz;  // Controlled_Buffer controlled_buffer_1
  assign controlled_buffer_1_out = not_1_out ? {16{1'b0}} : 16'bz;  // Controlled_Buffer controlled_buffer_2
  Shifter #(.width(16)) shifter_1 (.in(16'h1), .\dist (Bit_Select), .out(Mask));
  assign and_1_out = not_2_out & Data;  // AND_Gate and_1, 16 bits wide
  assign out_4 = controlled_buffer_1_out | and_1_out;  // OR_Gate or_1, 16 bits wide
endmodule
